# Fritzing sketch reciever (saved by Fritzing 0.9.3b)

parts:
  Часть1 = Arduino Nano (Rev3.0) (ICSP)
  Часть2 = NRF24L01+ Breakout Board
  U3 = RELAY [package=relay-jzc]
  LED1 = smd LED [color="Red (633nm)" package="0603 [SMD]"]
  VCC2 = Battery  # not connected
  VCC1 = Battery block 9V
  S2 = Pushbutton [package=THT]  # not connected
  LED2 = LEDs [package=led10mm]
  Part1 = KY-012 Active Buzzer Module [package="Breakout board"]  # not connected
  U4 = Voltage Regulator [package=sot223]
  IC1 = Voltage Regulator [package=78xxl]

nets:
  N1: Часть1.D5, LED2.C
  N2: Часть1.D6, U3.COIL2
  N3: Часть1.D9, Часть2.CE
  N4: Часть1.D10, Часть2.CS
  N5: Часть1.D11/MOSI, Часть2.MOSI
  N6: Часть1.D12/MISO, Часть2.MISO
  N7: Часть1.VIN, IC1.OUT
  N8: Часть1.D13/SCK, Часть2.SCK
  N9: Часть2.GND, U4.ADJ
  N10: Часть2.VCC, U4.OUT
  N11: U3.NO, VCC1.-, IC1.GND
  N12: U3.COIL1, LED1.cathode

notes:
  Ignitor
  3.3V
  7805
  2х18650

custom parts:
  KY-012 Active Buzzer Module: Active Piezoelectric Buzzer Module Keyes KY-012, it produces single-tone sound when signal is high.
