# Fritzing sketch transmitter (saved by Fritzing 0.9.3b)

parts:
  Часть1 = Arduino Nano (Rev3.0) (ICSP)
  Часть2 = NRF24L01+ Breakout Board
  VCC1 = Battery block 9V
  LED1 = LEDs [package=led10mm]
  LED2 = LEDs [package=led10mm]
  S3 = Pushbutton [package=THT]  # not connected
  S4 = Pushbutton [package="[SMD]"]
  U5 = Voltage Regulator [package=sot223]
  IC2 = Voltage Regulator [package=78xxl]
  R1 = Resistor [tolerance=±5% resistance=220 package="2512 [SMD]"]

nets:
  N1: Часть1.D4, S4.Pin_1, S4.Pin_2, R1.Pin_1
  N2: Часть1.D5, LED1.C
  N3: Часть1.D6, LED2.C
  N4: Часть1.D9, Часть2.CE
  N5: Часть1.D10, Часть2.CS
  N6: Часть1.D11/MOSI, Часть2.MOSI
  N7: Часть1.D12/MISO, Часть2.MISO
  N8: Часть1.VIN, IC2.OUT
  GND: Часть1.GND, VCC1.-, LED2.A, IC2.GND, R1.Pin_0
  N9: Часть1.5V, S4.Pin_3, S4.Pin_4
  N10: Часть1.D13/SCK, Часть2.SCK
  N11: Часть2.GND, U5.ADJ
  N12: Часть2.VCC, U5.OUT

notes:
  3.3V
  7805
